# Fritzing sketch ace128test (saved by Fritzing 0.9.3b)
breadboards: 1

parts:
  U1 = PCF8574 [package="DIP16 [THT]"]
  Part1 = Arduino Uno (Rev3)
  C1 = Ceramic Capacitor [capacitance=100nF package="100 mil [THT, multilayer]"]
  LCD1 = LCD screen
  R1 = Trimmer Potentiometer [maximum_resistance=10kΩ package=THT]
  R2 = Resistor [tolerance=±5% resistance=4.7k package=THT]
  R3 = Resistor [tolerance=±5% resistance=4.7k package=THT]
  U2 = ACE128 [package=ACE128]
  S1 = Pushbutton [package="[THT]"]

nets:
  VCC: U1.A0, U1.A1, U1.A3, U1.VCC, Part1.5V, C1.0, LCD1.VDD, R1.leg2, R2.Pin_0, R3.Pin_0
  N1: U1.P0, U2.1
  N2: U1.P1, U2.2
  N3: U1.P2, U2.8#3
  N4: U1.P3, U2.4
  GND: U1.GND, Part1.GND, C1.1, LCD1.VSS, LCD1.R/W, R1.leg1, U2.GND#2, S1.Pin_1, S1.Pin_2
  N5: U1.P4, U2.5
  N6: U1.P5, U2.6
  N7: U1.P6, U2.7
  N8: U1.P7, U2.8#9
  N9: U1.SCL, Part1.A5/SCL, R2.Pin_1
  N10: U1.SDA, Part1.A4/SDA, R3.Pin_1
  N11: Part1.D13/SCK, S1.Pin_3, S1.Pin_4
  N12: Part1.D2, LCD1.DB7
  N13: Part1.D3_PWM, LCD1.DB6
  N14: Part1.D4, LCD1.DB5
  N15: Part1.D5_PWM, LCD1.DB4
  N16: Part1.D6_PWM, LCD1.E
  N17: Part1.D7, LCD1.RS
  N18: LCD1.V0, R1.wiper
